# Fritzing sketch clock (saved by Fritzing 0.9.2b)
circuit board: 1.7617cm x 4.0381cm
breadboards: 1

parts:
  R1 = Resistor [tolerance=±5% resistance=220 package=THT]
  S1 = Pushbutton [package="[THT]"]
  LDR = PHOTOCELL [package=photocell]
  Part1 = Arduino Uno (Rev3)
  LPD8806_RGB_LED_Strip1 = LPD8806 RGB LED Strip
  Part2 = Real Time Clock Module - DS1307 RTC Breakout Board
  R2 = Resistor [tolerance=±5% resistance=220 package=THT]

nets:
  N1: R1.Pin_0, S1.Pin_1, S1.Pin_2, Part1.D4
  GND: R1.Pin_1, Part1.GND, LPD8806_RGB_LED_Strip1.GND, Part2.GND, R2.Pin_0
  5V: S1.Pin_3, S1.Pin_4, LDR.P$1, Part1.5V, LPD8806_RGB_LED_Strip1.+5V, Part2.5V
  N2: LDR.P$2, Part1.D1/TX, R2.Pin_1
  N3: Part1.A4/SDA, Part2.SDA
  N4: Part1.A5/SCL, Part2.SCL
  N5: Part1.D6_PWM, LPD8806_RGB_LED_Strip1.DI
  N6: Part1.D7, LPD8806_RGB_LED_Strip1.CI

notes:
  Sw
  5V
  GND
  Ph

custom parts:
  LPD8806 RGB LED Strip: Digitally addressable RGB LED strip
